// Logisim project bcd_divisibility.circ as structural Verilog: 8 circuits, main circuit main
module full_adder (
  input  A,
  input  B,
  input  Cin,
  output S,
  output Cout
);

  wire P1, P2, X1;

  xor xor_1 (X1, A, B);
  and and_1 (P1, A, B);
  xor xor_2 (S, X1, Cin);
  and and_2 (P2, X1, Cin);
  or or_1 (Cout, P1, P2);
endmodule

module adder4 (
  input  A0,
  input  B0,
  input  A1,
  input  B1,
  input  A2,
  input  B2,
  input  A3,
  input  B3,
  output S0,
  output S1,
  output S2,
  output S3,
  output S4
);

  wire CARRY1, CARRY2, CARRY3;

  full_adder FA0 (.A(A0), .B(B0), .Cin(1'b0), .S(S0), .Cout(CARRY1));
  full_adder FA1 (.A(A1), .B(B1), .Cin(CARRY1), .S(S1), .Cout(CARRY2));
  full_adder FA2 (.A(A2), .B(B2), .Cin(CARRY2), .S(S2), .Cout(CARRY3));
  full_adder FA3 (.A(A3), .B(B3), .Cin(CARRY3), .S(S3), .Cout(S4));
endmodule

module adder5 (
  input  A0,
  input  B0,
  input  A1,
  input  B1,
  input  A2,
  input  B2,
  input  A3,
  input  B3,
  input  A4,
  input  B4,
  output S0,
  output S1,
  output S2,
  output S3,
  output S4,
  output S5
);

  wire CARRY1, CARRY2, CARRY3, CARRY4;

  full_adder FA0 (.A(A0), .B(B0), .Cin(1'b0), .S(S0), .Cout(CARRY1));
  full_adder FA1 (.A(A1), .B(B1), .Cin(CARRY1), .S(S1), .Cout(CARRY2));
  full_adder FA2 (.A(A2), .B(B2), .Cin(CARRY2), .S(S2), .Cout(CARRY3));
  full_adder FA3 (.A(A3), .B(B3), .Cin(CARRY3), .S(S3), .Cout(CARRY4));
  full_adder FA4 (.A(A4), .B(B4), .Cin(CARRY4), .S(S4), .Cout(S5));
endmodule

module cmp3 (
  input  p1,
  input  p0,
  input  q1,
  input  q0,
  output Eq
);

  wire A0T, B0T, C0T, D0T, EQHI, EQLO, NP0, NP1, NQ0, NQ1, OR1, T1, T2, T3, XORHI, XORLO;

  xor xor_1 (XORHI, p1, q1);
  xor xor_2 (XORLO, p0, q0);
  not not_1 (NP1, p1);
  not not_2 (NP0, p0);
  not not_3 (NQ1, q1);
  not not_4 (NQ0, q0);
  not not_5 (EQHI, XORHI);
  not not_6 (EQLO, XORLO);
  and and_1 (A0T, NP1, NP0);
  and and_2 (B0T, q1, q0);
  and and_3 (C0T, p1, p0);
  and and_4 (D0T, NQ1, NQ0);
  and and_5 (T1, EQHI, EQLO);
  and and_6 (T2, A0T, B0T);
  and and_7 (T3, C0T, D0T);
  or or_1 (OR1, T1, T2);
  or or_2 (Eq, OR1, T3);
endmodule

module eq5 (
  input  A0,
  input  A1,
  input  A2,
  input  A3,
  input  A4,
  input  B0,
  input  B1,
  input  B2,
  input  B3,
  input  B4,
  output Eq
);

  wire N0, N1, N2, N3, N4, T1, T2, T3, X0, X1, X2, X3, X4;

  xor xor_1 (X0, A0, B0);
  xor xor_2 (X1, A1, B1);
  xor xor_3 (X2, A2, B2);
  xor xor_4 (X3, A3, B3);
  xor xor_5 (X4, A4, B4);
  not not_1 (N0, X0);
  not not_2 (N1, X1);
  not not_3 (N2, X2);
  not not_4 (N3, X3);
  not not_5 (N4, X4);
  and and_1 (T1, N0, N1);
  and and_2 (T2, N2, N3);
  and and_3 (T3, T1, T2);
  and and_4 (Eq, T3, N4);
endmodule

module mod3_checker (
  input  [3:0] D0,
  input  [3:0] D1,
  input  [3:0] D2,
  input  [3:0] D3,
  output out
);

  wire P0, P1, Q0, Q1, SAB0, SAB1, SAB2, SAB3, SAB4, SCD0, SCD1, SCD2, SCD3, SCD4, SUM0, SUM1, SUM2, SUM3,
       SUM4, SUM5;

  adder4 AB (
    .A0(D0[0]), .A1(D0[1]), .A2(D0[2]), .A3(D0[3]), .B0(D1[0]), .B1(D1[1]), .B2(D1[2]), .B3(D1[3]),
    .S0(SAB0), .S1(SAB1), .S2(SAB2), .S3(SAB3), .S4(SAB4));
  adder4 CD (
    .A0(D2[0]), .A1(D2[1]), .A2(D2[2]), .A3(D2[3]), .B0(D3[0]), .B1(D3[1]), .B2(D3[2]), .B3(D3[3]),
    .S0(SCD0), .S1(SCD1), .S2(SCD2), .S3(SCD3), .S4(SCD4));
  adder5 SUM (
    .A0(SAB0), .A1(SAB1), .A2(SAB2), .A3(SAB3), .A4(SAB4), .B0(SCD0), .B1(SCD1), .B2(SCD2), .B3(SCD3),
    .B4(SCD4), .S0(SUM0), .S1(SUM1), .S2(SUM2), .S3(SUM3), .S4(SUM4), .S5(SUM5));
  full_adder P (.A(SUM0), .B(SUM2), .Cin(SUM4), .S(P0), .Cout(P1));
  full_adder Q (.A(SUM1), .B(SUM3), .Cin(SUM5), .S(Q0), .Cout(Q1));
  cmp3 CMP (.p1(P1), .p0(P0), .q1(Q1), .q0(Q0), .Eq(out));

  // Other names for the same wires on the sheet: D0B0 = D0[0]; D0B1 = D0[1]; D0B2 = D0[2]; D0B3 = D0[3]; D1B0 = D1[0];
  //   D1B1 = D1[1]; D1B2 = D1[2]; D1B3 = D1[3]; D2B0 = D2[0]; D2B1 = D2[1]; D2B2 = D2[2]; D2B3 = D2[3]; D3B0 = D3[0];
  //   D3B1 = D3[1]; D3B2 = D3[2]; D3B3 = D3[3]

  // Notes on the sheet:
  //   mod3_checker: out=1 iff D3D2D1D0 (BCD) is a multiple of 3
endmodule

module mod11_checker (
  input  [3:0] D0,
  input  [3:0] D1,
  input  [3:0] D2,
  input  [3:0] D3,
  output out
);

  wire AA0, AA1, AA2, AA3, AA4, AP0, AP1, AP2, AP3, AP4, BB0, BB1, BB2, BB3, BB4, BP0, BP1, BP2, BP3, BP4,
       EQ1, EQ2, EQ3, OR1;

  adder4 A (
    .A0(D0[0]), .A1(D0[1]), .A2(D0[2]), .A3(D0[3]), .B0(D2[0]), .B1(D2[1]), .B2(D2[2]), .B3(D2[3]), .S0(AA0),
    .S1(AA1), .S2(AA2), .S3(AA3), .S4(AA4));
  adder4 B (
    .A0(D1[0]), .A1(D1[1]), .A2(D1[2]), .A3(D1[3]), .B0(D3[0]), .B1(D3[1]), .B2(D3[2]), .B3(D3[3]), .S0(BB0),
    .S1(BB1), .S2(BB2), .S3(BB3), .S4(BB4));
  adder5 AP11 (
    .A0(AA0), .A1(AA1), .A2(AA2), .A3(AA3), .A4(AA4), .B0(1'b1), .B1(1'b1), .B2(1'b0), .B3(1'b1), .B4(1'b0),
    .S0(AP0), .S1(AP1), .S2(AP2), .S3(AP3), .S4(AP4));  // open: S5
  adder5 BP11 (
    .A0(BB0), .A1(BB1), .A2(BB2), .A3(BB3), .A4(BB4), .B0(1'b1), .B1(1'b1), .B2(1'b0), .B3(1'b1), .B4(1'b0),
    .S0(BP0), .S1(BP1), .S2(BP2), .S3(BP3), .S4(BP4));  // open: S5
  eq5 u_EQ1 (
    .A0(AP0), .A1(AP1), .A2(AP2), .A3(AP3), .A4(AP4), .B0(BB0), .B1(BB1), .B2(BB2), .B3(BB3), .B4(BB4),
    .Eq(EQ1));
  eq5 u_EQ2 (
    .A0(AA0), .A1(AA1), .A2(AA2), .A3(AA3), .A4(AA4), .B0(BB0), .B1(BB1), .B2(BB2), .B3(BB3), .B4(BB4),
    .Eq(EQ2));
  eq5 u_EQ3 (
    .A0(AA0), .A1(AA1), .A2(AA2), .A3(AA3), .A4(AA4), .B0(BP0), .B1(BP1), .B2(BP2), .B3(BP3), .B4(BP4),
    .Eq(EQ3));
  or or_1 (OR1, EQ1, EQ2);
  or or_2 (out, OR1, EQ3);

  // Other names for the same wires on the sheet: D0B0 = D0[0]; D0B1 = D0[1]; D0B2 = D0[2]; D0B3 = D0[3]; D1B0 = D1[0];
  //   D1B1 = D1[1]; D1B2 = D1[2]; D1B3 = D1[3]; D2B0 = D2[0]; D2B1 = D2[1]; D2B2 = D2[2]; D2B3 = D2[3]; D3B0 = D3[0];
  //   D3B1 = D3[1]; D3B2 = D3[2]; D3B3 = D3[3]

  // Notes on the sheet:
  //   mod11_checker: out=1 iff D3D2D1D0 (BCD) is a multiple of 11
endmodule

module main (
  input  [3:0] D0,
  input  [3:0] D1,
  input  [3:0] D2,
  input  [3:0] D3,
  output mult_of_3,
  output mult_of_11
);

  mod3_checker MOD3 (.D0(D0), .D1(D1), .D2(D2), .D3(D3), .out(mult_of_3));
  mod11_checker MOD11 (.D0(D0), .D1(D1), .D2(D2), .D3(D3), .out(mult_of_11));

  // Notes on the sheet:
  //   BCD divisibility checkers (basic gates only) -- Lab 1
  //   D3 D2 D1 D0 = decimal digits (thousands..units), each 4-bit BCD
endmodule
