// Logisim project waiting_room.circ as structural Verilog: 1 circuit, main circuit waiting_room
module waiting_room (
  input  IN,
  input  OUT,
  input  Ent,
  input  T,
  input  Clk,
  input  Clr,
  output Open,
  output Close,
  output Q0,
  output Q1,
  output Q2,
  output Q3,
  output DBG_EN,
  output DBG_D0,
  output DBG_U
);

  wire and_3_out, and_4_out, and_6_out, and_7_out, and_8_out, D1, D2, D3, E0, NCLR, not_2_out, not_3_out,
       not_5_out, not_6_out, or_1_out, TOGGLE2, TOGGLE3, xor_1_out, xor_2_out, xor_3_out;

  xor ENABLE (DBG_EN, IN, OUT);
  not u_NCLR (NCLR, Clr);
  Register #(.width(1)) register_1 (.D(DBG_D0), .en(DBG_EN), .clk(Clk), .Q(Q0), .clr(NCLR));
  Register #(.width(1)) register_2 (.D(D1), .en(DBG_EN), .clk(Clk), .Q(Q1), .clr(NCLR));
  Register #(.width(1)) register_3 (.D(D2), .en(DBG_EN), .clk(Clk), .Q(Q2), .clr(NCLR));
  Register #(.width(1)) register_4 (.D(D3), .en(DBG_EN), .clk(Clk), .Q(Q3), .clr(NCLR));
  xor xor_1 (xor_1_out, Q0, IN);
  xor xor_2 (xor_2_out, Q1, IN);
  xor xor_3 (xor_3_out, Q2, IN);
  not not_1 (E0, xor_1_out);
  not not_2 (not_2_out, xor_2_out);
  and and_1 (TOGGLE2, E0, not_2_out);
  not not_3 (not_3_out, xor_3_out);
  and and_2 (TOGGLE3, TOGGLE2, not_3_out);
  not not_4 (DBG_D0, Q0);
  xor xor_4 (D1, Q1, E0);
  xor xor_5 (D2, Q2, TOGGLE2);
  xor xor_6 (D3, Q3, TOGGLE3);
  and and_3 (and_3_out, Q0, Q1);
  and and_4 (and_4_out, and_3_out, Q2);
  and and_5 (Close, and_4_out, Q3);
  not not_5 (not_5_out, Close);
  and and_6 (and_6_out, not_5_out, Ent);
  and and_7 (and_7_out, and_6_out, T);
  or or_1 (or_1_out, and_7_out, Open);
  not not_6 (not_6_out, IN);
  and and_8 (and_8_out, or_1_out, not_6_out);
  Register #(.width(1)) register_5 (.D(and_8_out), .en(1'b1), .clk(Clk), .Q(Open), .clr(NCLR));

  assign DBG_U = IN;

  // Other names for the same wires on the sheet: D0 = DBG_D0; ENABLE = DBG_EN; OPENQ = Open; U = IN
endmodule
